# Fritzing sketch project-beer (saved by Fritzing 0.9.5d)
breadboards: 4

parts:
  C1 = Ceramic Capacitor [capacitance=100nF package="100 mil [THT, multilayer]"]
  R2 = Resistor [tolerance=±5% resistance=3.3 package="0805 [SMD]"]
  esp1 = ESP32 DevKitc V4
  esp2 = ESP32 DevKitc V4
  Grove1 = Grove OLED 128x96
  LED1 = LEDs [package=led10mm]
  A1 = BBAA100043
  Matrix_keypad1 = KEYPAD 4x4
  DS2 = DS18B20 1-Wire Temperature Sensor Probe Cable
  R3 = Resistor [tolerance=±5% resistance=4.7 package="0805 [SMD]"]
  R4 = Resistor [tolerance=±5% resistance=4.7 package="0805 [SMD]"]
  R5 = Resistor [tolerance=±5% resistance=4.7 package="0805 [SMD]"]
  R6 = Resistor [tolerance=±5% resistance=220 package="0805 [SMD]"]

nets:
  N1: C1.0, R2.Pin_0, esp2.IO34
  N2: C1.1, A1.pin4, R6.Pin_0
  N3: R2.Pin_1, LED1.A
  N4: esp1.IO32, Matrix_keypad1.col1
  N5: esp1.IO33, Matrix_keypad1.col2
  N6: esp1.IO25, Matrix_keypad1.col3
  N7: esp1.IO26, Matrix_keypad1.col4
  N8: esp1.IO27, Matrix_keypad1.row1
  N9: esp1.IO14, Matrix_keypad1.row2
  N10: esp1.IO12, Matrix_keypad1.row3
  N11: esp1.IO13, Matrix_keypad1.row4
  N12: esp2.IO21, Grove1.SDA, R4.Pin_1
  N13: esp2.IO22, Grove1.SCL, R5.Pin_0
  N14: esp2.GND#18, Grove1.GND
  N15: Grove1.VCC, R4.Pin_0, R5.Pin_1
  N16: LED1.C, R6.Pin_1
  N17: DS2.VDD, R3.Pin_0
  N18: DS2.shield, R3.Pin_1

custom parts:
  ESP32 DevKitc V4: ESP32-DevKitC board with ESP32-WROOM-32 module. ESP32-DevKitC V4 is a small-sized ESP32-based development board produced by Espressif. Most of the pins on the ESP module are broken out to the pin headers on the board. The pins D0, D1, D2, D3, CMD and CLK are used internally for communication between ESP32 and SPI flash memory. They are grouped on both sides near the USB connector. Avoid using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
  BBAA100043: BBAA100043 traffic light module.
  KEYPAD 4x4: Matrix keypad 16 buttons, 4 rows x 4 columns

// code stored in the sketch: project-beer.ino

